# Fritzing sketch Circuit_Layout (saved by Fritzing 0.9.3b)
circuit board: 8.46667cm x 5.64444cm
breadboards: 1

parts:
  Part1 = Arduino Uno (Rev3) - ICSP
  J1 = Basic Servo
  J2 = Basic Servo
  J3 = Basic Servo

nets:
  VCC: Part1.5V, J1.vcc, J2.vcc, J3.vcc
  N1: Part1.ICSP_MOSI, Part1.D11_PWM/MOSI, J3.pulse
  GND: Part1.GND, J1.gnd, J2.gnd, J3.gnd
  N2: Part1.D9_PWM, J2.pulse
  N3: Part1.D10_PWM/SS, J1.pulse
